# Fritzing sketch weather (saved by Fritzing 0.9.3b)
breadboards: 1

parts:
  U1 = NodeMCU V1.0
  Bauteil1 = Barometric Pressure Sensor - BMP180 Breakout (GY-68)
  DS1 = DS18B20 1-Wire Temperature Sensor [part_number=DS18B20]
  S1 = Momentary Switch [package=tactile-pth]
  DHT1 = DHT22 Humidity and Temperature Sensor
  VCC1 = Battery
  JP1 = USB_MICROB_PLUG [package=micro-b-ra-th]

nets (from the breadboard view):
  N1: U1.D4, DHT1.DATA
  VDD: U1.3V3, Bauteil1.VCC, DS1.VDD, DHT1.VDD
  GND: U1.GND, Bauteil1.GND, DS1.GND, S1.1, DHT1.GND
  N2: U1.D5, DS1.DQ
  N3: U1.D6, Bauteil1.SDA
  N4: U1.D7, Bauteil1.SCL
  N5: U1.RST, S1.2
  N6: VCC1.+, JP1.VCC

notes:
  3x1,5V via Micro USB
  DHT22, DS18B20, BMP180

custom parts:
  NodeMCU V1.0: ESP9266 based NodeMCU
